# Fritzing sketch LM358synth (saved by Fritzing 0.9.3b)
circuit board: 8.46667cm x 5.64444cm
breadboards: 1

parts:
  IC1 = IC, DIP package, 8 pins [chip_label="LM358 1"]
  R5 = Resistor [tolerance=±5% resistance=100k package=THT]
  VCC1 = Battery block 9V
  R4 = Resistor [tolerance=±5% resistance=100k package=THT]
  R1 = Resistor [tolerance=±5% resistance=47k package=THT]
  R2 = Resistor [tolerance=±5% resistance=22k package=THT]
  S1 = Momentary Switch [package=ksa_sealed_tac_switch]
  R16_note = Rotary Potentiometer (Small) [maximum_resistance=100kΩ package=THT]
  R3 = Resistor [tolerance=±5% resistance=10k package=THT]
  C1 = Ceramic Capacitor [capacitance=4.7mF package="100 mil [THT, multilayer]"]
  IC3 = IC, DIP package, 8 pins [chip_label=LM358]
  IC2 = IC, DIP package, 8 pins [chip_label=LM358]
  C2 = Electrolytic Capacitor [capacitance=1µF package="100 mil [THT, electrolytic]"]
  R7 = Resistor [tolerance=±5% resistance=22k package=THT]
  R6 = Resistor [tolerance=±5% resistance=47k package=THT]
  R8 = Resistor [tolerance=±5% resistance=470k package=THT]
  R9 = Resistor [tolerance=±5% resistance=100k package=THT]
  R10 = Resistor [tolerance=±5% resistance=100k package=THT]
  IC4 = IC, DIP package, 8 pins [chip_label=LM358]
  IC5 = IC, DIP package, 8 pins [chip_label=LM358]
  R13_pwm = Rotary Potentiometer (Small) [maximum_resistance=100kΩ package=THT]
  C3 = Electrolytic Capacitor [capacitance=1µF package="100 mil [THT, electrolytic]"]
  R31 = Resistor [tolerance=±5% resistance=47k package=THT]
  R12 = Resistor [tolerance=±5% resistance=100k package=THT]
  R11 = Resistor [tolerance=±5% resistance=22k package=THT]
  R14 = Resistor [tolerance=±5% resistance=47k package=THT]
  R15 = Resistor [tolerance=±5% resistance=4.7k package=THT]
  R28 = Resistor [tolerance=±5% resistance=22k package=THT]
  LDR1 = Photocell (LDR) [package=THT]
  LDR2 = Photocell (LDR) [package=THT]
  R24 = Resistor [tolerance=±5% resistance=10k package=THT]
  R25 = Resistor [tolerance=±5% resistance=10k package=THT]
  C4 = Ceramic Capacitor [capacitance="100 nF" package="0603 [SMD, multilayer]"]
  R30 = Resistor [tolerance=±5% resistance=22k package=THT]
  C5 = Ceramic Capacitor [capacitance="100 nF" package="0603 [SMD, multilayer]"]
  R32 = Resistor [tolerance=±5% resistance=10k package=THT]
  R27 = Resistor [tolerance=±5% resistance=100k package=THT]
  R26 = Resistor [tolerance=±5% resistance=100k package=THT]
  C6 = Electrolytic Capacitor [capacitance=1µF package="100 mil [THT, electrolytic]"]
  TRS1 = Audio Jack (TRS) 3.5mm [package="4Ucon 08780 [THT]"]
  R40 = Resistor [tolerance=±5% resistance=22k package=THT]

nets:
  N1: IC1.pin1, R1.Pin_0, S1.2
  N2: IC1.pin2, IC1.pin5, R5.Pin_0, R4.Pin_1
  N3: IC1.pin3, R1.Pin_1, R2.Pin_0
  N4: IC1.pin4, R5.Pin_1, VCC1.-, R16_note.leg1, IC3.pin4, IC2.pin4, R10.Pin_1, IC4.pin4, IC5.pin4, IC5.pin5, R13_pwm.leg1, R15.Pin_1, R27.Pin_1, TRS1.Sleeve, R40.Pin_1
  N5: IC1.pin6, R3.Pin_0, C1.1
  N6: IC1.pin7, R2.Pin_1, C1.0, IC3.pin2
  N7: IC1.pin8, VCC1.+, R4.Pin_0, IC3.pin8, IC2.pin2, IC2.pin5, IC2.pin8, R9.Pin_0, R9.Pin_1, R10.Pin_0, IC4.pin8, IC5.pin8, R13_pwm.leg2, R26.Pin_0
  N8: S1.1, R16_note.wiper
  N9: R16_note.leg2, R3.Pin_1
  N10: IC3.pin1, R14.Pin_0
  N11: IC3.pin3, IC3.pin7, R11.Pin_0
  N12: IC3.pin5, R13_pwm.wiper
  N13: IC3.pin6, R12.Pin_1, R11.Pin_1
  N14: IC2.pin1, R6.Pin_0, R8.Pin_0
  N15: IC2.pin3, R7.Pin_0, R6.Pin_1
  N16: IC2.pin6, C2.+, R8.Pin_1
  N17: IC2.pin7, C2.-, R7.Pin_1, R12.Pin_0
  N18: IC4.pin1, IC4.pin2, LDR2.pin_0, C4.0, C4.1
  N19: IC4.pin3, IC5.pin3, R27.Pin_0, R26.Pin_1
  N20: IC4.pin5, R31.Pin_1
  N21: IC4.pin6, R28.Pin_0, R30.Pin_0
  N22: IC4.pin7, R28.Pin_1, LDR1.pin_1
  N23: IC5.pin1, R30.Pin_1, C5.1, R32.Pin_0
  N24: IC5.pin2, R25.Pin_1, C5.0
  N25: IC5.pin6, IC5.pin7
  N26: C3.-, R14.Pin_1, R15.Pin_0
  N27: C3.+, R31.Pin_0
  N28: LDR1.pin_0, R24.Pin_0
  N29: LDR2.pin_1, R25.Pin_0
  N30: R32.Pin_1, C6.-
  N31: C6.+, TRS1.Ring, TRS1.Tip, R40.Pin_0
